# Fritzing sketch MIDILemons Board (saved by Fritzing 0.9.2b)
breadboards: 1

parts:
  Arduino_Nano = Arduino Nano (Rev3.0)
  DIP_Switch_for_Configuration = DIP SWITCH [package=dipswitch-02]
  SW2 = DIP SWITCH [package=dipswitch-02]
  Sensitivity_Potentiometer_(10K_ohm) = POT [package=3362u]
  R13 = Resistor [tolerance=±5% resistance=1M package=THT]
  Capacitive_Input_(Lemons) = Screw terminal - 2 pins [package=THT]
  R2 = Resistor [tolerance=±5% resistance=1M package=THT]
  R3 = Resistor [tolerance=±5% resistance=1M package=THT]
  R4 = Resistor [tolerance=±5% resistance=1M package=THT]
  J2 = Screw terminal - 2 pins [package=THT]
  R5 = Resistor [tolerance=±5% resistance=1M package=THT]
  R6 = Resistor [tolerance=±5% resistance=1M package=THT]
  J3 = Screw terminal - 2 pins [package=THT]
  R7 = Resistor [tolerance=±5% resistance=1M package=THT]
  R8 = Resistor [tolerance=±5% resistance=1M package=THT]
  J4 = Screw terminal - 2 pins [package=THT]
  R9 = Resistor [tolerance=±5% resistance=1M package=THT]
  R10 = Resistor [tolerance=±5% resistance=1M package=THT]
  J5 = Screw terminal - 2 pins [package=THT]
  R11 = Resistor [tolerance=±5% resistance=1M package=THT]
  R12 = Resistor [tolerance=±5% resistance=1M package=THT]
  J6 = Screw terminal - 2 pins [package=THT]

nets:
  N1: Arduino_Nano.D1/TX, R11.Pin_1, J6.pin1
  N2: Arduino_Nano.D0/RX, R12.Pin_1, J6.pin2
  N3: Arduino_Nano.GND, DIP_Switch_for_Configuration.3, DIP_Switch_for_Configuration.4, SW2.3, SW2.4, Sensitivity_Potentiometer_(10K_ohm).A
  N4: Arduino_Nano.D2, R10.Pin_1, J5.pin2
  N5: Arduino_Nano.D3, R9.Pin_1, J5.pin1
  N6: Arduino_Nano.D4, R8.Pin_1, J4.pin2
  N7: Arduino_Nano.D5, R7.Pin_1, J4.pin1
  N8: Arduino_Nano.D6, R6.Pin_1, J3.pin2
  N9: Arduino_Nano.D7, R5.Pin_1, J3.pin1
  N10: Arduino_Nano.D8, R4.Pin_1, J2.pin2
  N11: Arduino_Nano.D9, R3.Pin_1, J2.pin1
  N12: Arduino_Nano.D10, Capacitive_Input_(Lemons).pin2, R2.Pin_1
  N13: Arduino_Nano.D11/MOSI, R13.Pin_1, Capacitive_Input_(Lemons).pin1
  N14: Arduino_Nano.D12/MISO, R13.Pin_0, R2.Pin_0, R3.Pin_0, R4.Pin_0, R5.Pin_0, R6.Pin_0, R7.Pin_0, R8.Pin_0, R9.Pin_0, R10.Pin_0, R11.Pin_0, R12.Pin_0
  N15: Arduino_Nano.A7, SW2.1
  N16: Arduino_Nano.A6, SW2.2
  N17: Arduino_Nano.A5, DIP_Switch_for_Configuration.1
  N18: Arduino_Nano.A4, DIP_Switch_for_Configuration.2
  N19: Arduino_Nano.A0, Sensitivity_Potentiometer_(10K_ohm).S
  N20: Arduino_Nano.3V3, Sensitivity_Potentiometer_(10K_ohm).E
