# Fritzing sketch MovementLight (saved by Fritzing 0.9.2b)
breadboards: 1

parts:
  R5 = Resistor [tolerance=±5% resistance=100 package=THT]
  LED2 = LED - 3mm [color="Red (633nm)" package="3 mm [THT]"]
  LED3 = LED - 3mm [color="Red (633nm)" package="3 mm [THT]"]
  LED4 = LED - 3mm [color="Red (633nm)" package="3 mm [THT]"]
  LED5 = LED - 3mm [color="Red (633nm)" package="3 mm [THT]"]
  LED6 = LED - 3mm [color="Red (633nm)" package="3 mm [THT]"]
  LED7 = LED - 3mm [color="Red (633nm)" package="3 mm [THT]"]
  LED8 = LED - 3mm [color="Red (633nm)" package="3 mm [THT]"]
  LED9 = LED - 3mm [color="Red (633nm)" package="3 mm [THT]"]
  R2 = Resistor [tolerance=±5% resistance=220 package=THT]
  R3 = Resistor [tolerance=±5% resistance=220 package=THT]
  R4 = Photocell (LDR) [package=THT]
  part = Resistor [tolerance=±5% resistance=10k package=THT]
  Q1 = NPN-Transistor [package="SOT-23 [SMD]"]
  ATMega8 = MICROCONTROLLER [package=dil28-3-simon-kit]
  LED = LED - 5mm [color="White (6500K)" package="5 mm [THT]"]
  12v = 4 x AAA Battery Mount
  10kΩ = TRIMPOT [package=trimpot_tc33]
  LM7805 = Voltage Regulator - 5V [package="DPak [SMD]"]
  C1 = Electrolytic Capacitor [capacitance=47µF package="300 mil [THT, electrolytic]"]
  C2 = Electrolytic Capacitor [capacitance=10µF package="300 mil [THT, electrolytic]"]
  Lhi1 = LHi958 [package=to-39]

nets:
  N1: R5.Pin_0, LED2.cathode, LED.cathode
  N2: R5.Pin_1, R2.Pin_1, R3.Pin_1, Q1.1
  N3: LED2.anode, LED3.cathode
  N4: LED3.anode, LED6.anode, LED9.anode, 12v.+, LM7805.input_voltage, C1.+
  N5: LED4.cathode, R2.Pin_0
  N6: LED4.anode, LED5.cathode
  N7: LED5.anode, LED6.cathode
  N8: LED7.cathode, R3.Pin_0
  N9: LED7.anode, LED8.cathode
  N10: LED8.anode, LED9.cathode
  N11: R4.pin_0, ATMega8.VCC, 10kΩ.CCW, LM7805.output_voltage, C2.+, Lhi1.n.a.
  N12: R4.pin_1, part.Pin_0, ATMega8.PB1(OC1A)
  GND: part.Pin_1, Q1.2, ATMega8.GND, 12v.-, 10kΩ.CW, LM7805.GND, C1.-, C2.-, Lhi1.GND
  N13: Q1.0, ATMega8.PB3(MOSI_OC2)
  N14: ATMega8.PB0(ICP), 10kΩ.WIPER
  N15: ATMega8.PB2(SS_OC1B), Lhi1.D
